# Fritzing sketch Kaavio (saved by Fritzing 0.9.3b)
breadboards: 1

parts:
  Part1 = Arduino Mega 2560 (Rev3)
  LED1 = LED - 5mm [color="Red (633nm)" package="5 mm [THT]"]
  R1 = Resistor [tolerance=±5% resistance=220 package=THT]
  S1 = Pushbutton [package="[SMD]"]

nets:
  N1: Part1.GND, LED1.cathode, S1.Pin_3, S1.Pin_4
  N2: Part1.D13_PWM, R1.Pin_1
  N3: Part1.D2_PWM, S1.Pin_1, S1.Pin_2
  N4: LED1.anode, R1.Pin_0
